// Logisim project Lab_2_Part_III_Solution.circ as structural Verilog: 6 circuits, main circuit main
module main (
  input  in_1,
  input  in_2,
  input  in_3,
  input  in_4,
  input  in_5,
  input  in_6,
  input  in_7,
  input  in_8,
  input  in_9
);

  wire CircuitA_1_o0, CircuitA_1_o1, CircuitA_1_o2, cout, d0, d1, d2, d3, d4, d5, d6, e0, e1, e2, e3,
       full_adder_2_co, full_adder_3_co, full_adder_4_co, hello, multiplexer_1_out, multiplexer_2_out,
       multiplexer_3_out, multiplexer_4_out, s0, s1, s2, s3, s4, s5, s6, z;
  wire [7:7] Seg7_Decoder_1_o_seg;

  Full_Adder full_adder_1 (.ci(full_adder_2_co), .a(in_8), .b(in_9), .s(e3), .co(cout));
  Full_Adder full_adder_2 (.ci(full_adder_3_co), .a(in_6), .b(in_7), .s(e2), .co(full_adder_2_co));
  Full_Adder full_adder_3 (.ci(full_adder_4_co), .a(in_4), .b(in_5), .s(e1), .co(full_adder_3_co));
  Full_Adder full_adder_4 (.ci(in_3), .a(in_1), .b(in_2), .s(e0), .co(full_adder_4_co));
  or or_1 (z, cout, hello);
  myComparator myComparator_1 (.v3(e3), .v2(e2), .v1(e1), .v0(e0), .z(hello));
  CircuitA CircuitA_1 (.i2(e2), .i1(e1), .i0(e0), .o2(CircuitA_1_o2), .o1(CircuitA_1_o1), .o0(CircuitA_1_o0));
  Multiplexer multiplexer_1 (.in0(e3), .out(multiplexer_1_out), .sel(z));  // open: in1
  Multiplexer multiplexer_2 (.in0(e2), .in1(CircuitA_1_o2), .out(multiplexer_2_out), .sel(z));
  Multiplexer multiplexer_3 (.in0(e1), .in1(CircuitA_1_o1), .out(multiplexer_3_out), .sel(z));
  Multiplexer multiplexer_4 (.in0(e0), .in1(CircuitA_1_o0), .out(multiplexer_4_out), .sel(z));
  _7_Segment_Display #(.active("false")) L_7_Segment_Display_2 (
    .g(s6), .f(s5), .a(s0), .b(s1), .e(s4), .d(s3), .c(s2), .dp(1'b1));
  _7_Segment_Display #(.active("false")) L_7_Segment_Display_1 (
    .g(d6), .f(d5), .a(d0), .b(d1), .e(d4), .d(d3), .c(d2), .dp(1'b1));
  CircuitB CircuitB_1 (.z(z), .s6(d6), .s5(d5), .s4(d4), .s3(d3), .s2(d2), .s1(d1), .s0(d0));
  Seg7_Decoder Seg7_Decoder_1 (
    .i_m3(multiplexer_1_out), .i_m2(multiplexer_2_out), .i_m1(multiplexer_3_out), .i_m0(multiplexer_4_out),
    .o_seg({Seg7_Decoder_1_o_seg[7], s6, s5, s4, s3, s2, s1, s0}));

  // Other names for the same wires on the sheet: a0 = in_1; a1 = in_4; a2 = in_6; a3 = in_8; b0 = in_2; b1 = in_5;
  //   b2 = in_7; b3 = in_9; cin = in_3
endmodule

module Seg7_Decoder (
  input  i_m3,
  input  i_m2,
  input  i_m1,
  input  i_m0,
  output [7:0] o_seg
);

  wire and_1_out, and_2_out, and_3_out, and_4_out, and_5_out, and_6_out, and_7_out, and_8_out, and_10_out,
       and_11_out, and_12_out, and_13_out, not_1_out, not_2_out, not_3_out, not_4_out;

  not not_1 (not_1_out, i_m3);
  not not_2 (not_2_out, i_m2);
  not not_3 (not_3_out, i_m1);
  not not_4 (not_4_out, i_m0);
  and and_1 (and_1_out, not_1_out, not_2_out, not_3_out);
  and and_2 (and_2_out, i_m2, i_m1, i_m0);
  and and_3 (and_3_out, not_1_out, not_2_out, i_m0);
  and and_4 (and_4_out, not_2_out, i_m1);
  and and_5 (and_5_out, i_m2, not_3_out);
  and and_6 (and_6_out, not_1_out, not_2_out, not_3_out, i_m0);
  and and_7 (and_7_out, i_m2, not_3_out, not_4_out);
  and and_8 (and_8_out, i_m2, i_m1, i_m0);
  and and_9 (o_seg[2], not_2_out, i_m1, not_4_out);
  and and_10 (and_10_out, i_m2, not_3_out, i_m0);
  and and_11 (and_11_out, i_m2, i_m1, not_4_out);
  and and_12 (and_12_out, not_1_out, not_2_out, not_3_out, i_m0);
  and and_13 (and_13_out, i_m2, not_3_out, not_4_out);
  or or_1 (o_seg[6], and_1_out, and_2_out);
  or or_2 (o_seg[5], and_3_out, and_4_out);
  or or_3 (o_seg[4], i_m0, and_5_out);
  or or_4 (o_seg[3], and_6_out, and_7_out, and_8_out);
  or or_5 (o_seg[1], and_10_out, and_11_out);
  or or_6 (o_seg[0], and_12_out, and_13_out);

  assign o_seg[7] = 1'b1;
endmodule

module CircuitA (
  input  i2,
  input  i1,
  input  i0,
  output o2,
  output o1,
  output o0
);

  not not_1 (o1, i1);
  and and_1 (o2, i2, i1);

  assign o0 = i0;
endmodule

module myComparator (
  input  v3,
  input  v2,
  input  v1,
  input  v0,
  output z
);

  wire and_1_out, and_2_out;

  and and_1 (and_1_out, v3, v1);
  and and_2 (and_2_out, v3, v2);
  or or_1 (z, and_1_out, and_2_out);
endmodule

module CircuitB (
  input  z,
  output s6,
  output s5,
  output s4,
  output s3,
  output s2,
  output s1,
  output s0
);


  assign s0 = z;
  assign s1 = 1'b0;
  assign s2 = 1'b0;
  assign s3 = z;
  assign s4 = z;
  assign s5 = z;
  assign s6 = 1'b1;
endmodule

module Full_Adder (
  input  ci,
  input  a,
  input  b,
  output s,
  output co
);

  wire and_1_out, and_2_out, and_3_out, and_4_out, and_5_out, and_6_out, and_7_out, not_1_out, not_2_out,
       not_3_out;

  not not_1 (not_1_out, ci);
  not not_2 (not_2_out, a);
  not not_3 (not_3_out, b);
  and and_1 (and_1_out, not_1_out, not_2_out, b);
  and and_2 (and_2_out, not_1_out, a, not_3_out);
  and and_3 (and_3_out, ci, not_2_out, not_3_out);
  and and_4 (and_4_out, ci, a, b);
  and and_5 (and_5_out, a, b);
  and and_6 (and_6_out, ci, b);
  and and_7 (and_7_out, ci, a);
  or or_1 (s, and_1_out, and_2_out, and_3_out, and_4_out);
  or or_2 (co, and_5_out, and_6_out, and_7_out);
endmodule
