// Logisim project Lab_2_Part_IV_Solution.circ as structural Verilog: 7 circuits, main circuit main
module main (
  input  in_1,
  input  in_2,
  input  in_3,
  input  in_4,
  input  in_5,
  input  in_6,
  input  in_7,
  input  in_8,
  input  in_9
);

  wire bcd_adder_1_cout, d0, d1, d2, d3, d4, d5, d6, s0, s1, s2, s3, s4, s5, s6;
  wire [3:0] bcd_adder_1_s;
  wire [7:7] Seg7_Decoder_1_o_seg;

  BCD_Adder bcd_adder_1 (
    .Cin(in_3), .A({in_8, in_6, in_4, in_1}), .B({in_9, in_7, in_5, in_2}), .cout(bcd_adder_1_cout),
    .S(bcd_adder_1_s));
  _7_Segment_Display #(.active("false")) L_7_Segment_Display_1 (
    .g(d6), .f(d5), .a(d0), .b(d1), .e(d4), .d(d3), .c(d2), .dp(1'b1));
  CircuitB CircuitB_1 (.z(bcd_adder_1_cout), .s6(d6), .s5(d5), .s4(d4), .s3(d3), .s2(d2), .s1(d1), .s0(d0));
  Seg7_Decoder Seg7_Decoder_1 (
    .i_m3(bcd_adder_1_s[3]), .i_m2(bcd_adder_1_s[2]), .i_m1(bcd_adder_1_s[1]), .i_m0(bcd_adder_1_s[0]),
    .o_seg({Seg7_Decoder_1_o_seg[7], s6, s5, s4, s3, s2, s1, s0}));
  _7_Segment_Display #(.active("false")) L_7_Segment_Display_2 (
    .g(s6), .f(s5), .a(s0), .b(s1), .e(s4), .d(s3), .c(s2), .dp(1'b1));

  // Other names for the same wires on the sheet: a0 = in_1; a1 = in_4; a2 = in_6; a3 = in_8; b0 = in_2; b1 = in_5;
  //   b2 = in_7; b3 = in_9; cin = in_3
endmodule

module Seg7_Decoder (
  input  i_m3,
  input  i_m2,
  input  i_m1,
  input  i_m0,
  output [7:0] o_seg
);

  wire and_1_out, and_2_out, and_3_out, and_4_out, and_5_out, and_6_out, and_7_out, and_8_out, and_10_out,
       and_11_out, and_12_out, and_13_out, not_1_out, not_2_out, not_3_out, not_4_out;

  not not_1 (not_1_out, i_m3);
  not not_2 (not_2_out, i_m2);
  not not_3 (not_3_out, i_m1);
  not not_4 (not_4_out, i_m0);
  and and_1 (and_1_out, not_1_out, not_2_out, not_3_out);
  and and_2 (and_2_out, i_m2, i_m1, i_m0);
  and and_3 (and_3_out, not_1_out, not_2_out, i_m0);
  and and_4 (and_4_out, not_2_out, i_m1);
  and and_5 (and_5_out, i_m2, not_3_out);
  and and_6 (and_6_out, not_1_out, not_2_out, not_3_out, i_m0);
  and and_7 (and_7_out, i_m2, not_3_out, not_4_out);
  and and_8 (and_8_out, i_m2, i_m1, i_m0);
  and and_9 (o_seg[2], not_2_out, i_m1, not_4_out);
  and and_10 (and_10_out, i_m2, not_3_out, i_m0);
  and and_11 (and_11_out, i_m2, i_m1, not_4_out);
  and and_12 (and_12_out, not_1_out, not_2_out, not_3_out, i_m0);
  and and_13 (and_13_out, i_m2, not_3_out, not_4_out);
  or or_1 (o_seg[6], and_1_out, and_2_out);
  or or_2 (o_seg[5], and_3_out, and_4_out);
  or or_3 (o_seg[4], i_m0, and_5_out);
  or or_4 (o_seg[3], and_6_out, and_7_out, and_8_out);
  or or_5 (o_seg[1], and_10_out, and_11_out);
  or or_6 (o_seg[0], and_12_out, and_13_out);

  assign o_seg[7] = 1'b1;
endmodule

module CircuitA (
  input  i2,
  input  i1,
  input  i0,
  output o2,
  output o1,
  output o0
);

  not not_1 (o1, i1);
  and and_1 (o2, i2, i1);

  assign o0 = i0;
endmodule

module myComparator (
  input  v3,
  input  v2,
  input  v1,
  input  v0,
  output z
);

  wire and_1_out, and_2_out;

  and and_1 (and_1_out, v3, v1);
  and and_2 (and_2_out, v3, v2);
  or or_1 (z, and_1_out, and_2_out);
endmodule

module CircuitB (
  input  z,
  output s6,
  output s5,
  output s4,
  output s3,
  output s2,
  output s1,
  output s0
);


  assign s0 = z;
  assign s1 = 1'b0;
  assign s2 = 1'b0;
  assign s3 = z;
  assign s4 = z;
  assign s5 = z;
  assign s6 = 1'b1;
endmodule

module Full_Adder (
  input  ci,
  input  a,
  input  b,
  output s,
  output co
);

  wire and_1_out, and_2_out, and_3_out, and_4_out, and_5_out, and_6_out, and_7_out, not_1_out, not_2_out,
       not_3_out;

  not not_1 (not_1_out, ci);
  not not_2 (not_2_out, a);
  not not_3 (not_3_out, b);
  and and_1 (and_1_out, not_1_out, not_2_out, b);
  and and_2 (and_2_out, not_1_out, a, not_3_out);
  and and_3 (and_3_out, ci, not_2_out, not_3_out);
  and and_4 (and_4_out, ci, a, b);
  and and_5 (and_5_out, a, b);
  and and_6 (and_6_out, ci, b);
  and and_7 (and_7_out, ci, a);
  or or_1 (s, and_1_out, and_2_out, and_3_out, and_4_out);
  or or_2 (co, and_5_out, and_6_out, and_7_out);
endmodule

module BCD_Adder (
  input  Cin,
  input  [3:0] A,
  input  [3:0] B,
  output cout,
  output [3:0] S
);

  wire circuita_1_o0, circuita_1_o1, circuita_1_o2, full_adder_1_co, full_adder_1_s, full_adder_2_co,
       full_adder_2_s, full_adder_3_co, full_adder_3_s, full_adder_4_co, full_adder_4_s, mycomparator_1_z;

  Full_Adder full_adder_1 (.ci(Cin), .a(A[0]), .b(B[0]), .s(full_adder_1_s), .co(full_adder_1_co));
  CircuitA circuita_1 (
    .i2(full_adder_3_s), .i1(full_adder_2_s), .i0(full_adder_1_s), .o2(circuita_1_o2), .o1(circuita_1_o1),
    .o0(circuita_1_o0));
  Multiplexer multiplexer_1 (.in0(full_adder_1_s), .in1(circuita_1_o0), .out(S[0]), .sel(cout));
  Full_Adder full_adder_2 (.ci(full_adder_1_co), .a(A[1]), .b(B[1]), .s(full_adder_2_s), .co(full_adder_2_co));
  Multiplexer multiplexer_2 (.in0(full_adder_2_s), .in1(circuita_1_o1), .out(S[1]), .sel(cout));
  Multiplexer multiplexer_3 (.in0(full_adder_3_s), .in1(circuita_1_o2), .out(S[2]), .sel(cout));
  Full_Adder full_adder_3 (.ci(full_adder_2_co), .a(A[2]), .b(B[2]), .s(full_adder_3_s), .co(full_adder_3_co));
  or or_1 (cout, mycomparator_1_z, full_adder_4_co);
  Multiplexer multiplexer_4 (.in0(full_adder_4_s), .in1(1'b0), .out(S[3]), .sel(cout));
  Multiplexer multiplexer_5 (.in0(full_adder_4_s), .in1(1'b0), .out(S[3]), .sel(cout));
  Full_Adder full_adder_4 (.ci(full_adder_3_co), .a(A[3]), .b(B[3]), .s(full_adder_4_s), .co(full_adder_4_co));
  myComparator mycomparator_1 (
    .v3(full_adder_4_s), .v2(full_adder_3_s), .v1(full_adder_2_s), .v0(full_adder_1_s), .z(mycomparator_1_z));
endmodule
