// Logisim project Lab_2_Part_V_Solution.circ as structural Verilog: 8 circuits, main circuit main
module main (
  input  v3,
  input  v2,
  input  v1,
  input  v0
);

  wire CircuitA_1_o0, CircuitA_1_o1, CircuitA_1_o2, d0, d1, d2, d3, d4, d5, d6, multiplexer_1_out,
       multiplexer_2_out, multiplexer_3_out, multiplexer_4_out, s0, s1, s2, s3, s4, s5, s6, z;
  wire [7:7] Seg7_Decoder_1_o_seg;

  CircuitA CircuitA_1 (.i2(v2), .i1(v1), .i0(v0), .o2(CircuitA_1_o2), .o1(CircuitA_1_o1), .o0(CircuitA_1_o0));
  myComparator myComparator_1 (.v3(v3), .v2(v2), .v1(v1), .v0(v0), .z(z));
  Multiplexer multiplexer_1 (.in0(v3), .out(multiplexer_1_out), .sel(z));  // open: in1
  Multiplexer multiplexer_2 (.in0(v2), .in1(CircuitA_1_o2), .out(multiplexer_2_out), .sel(z));
  Multiplexer multiplexer_3 (.in0(v1), .in1(CircuitA_1_o1), .out(multiplexer_3_out), .sel(z));
  Multiplexer multiplexer_4 (.in0(v0), .in1(CircuitA_1_o0), .out(multiplexer_4_out), .sel(z));
  CircuitB CircuitB_1 (.z(z), .s6(d6), .s5(d5), .s4(d4), .s3(d3), .s2(d2), .s1(d1), .s0(d0));
  Seg7_Decoder Seg7_Decoder_1 (
    .i_m3(multiplexer_1_out), .i_m2(multiplexer_2_out), .i_m1(multiplexer_3_out), .i_m0(multiplexer_4_out),
    .o_seg({Seg7_Decoder_1_o_seg[7], s6, s5, s4, s3, s2, s1, s0}));
  _7_Segment_Display #(.active("false")) L_7_Segment_Display_1 (
    .g(d6), .f(d5), .a(d0), .b(d1), .e(d4), .d(d3), .c(d2), .dp(1'b1));
  _7_Segment_Display #(.active("false")) L_7_Segment_Display_2 (
    .g(s6), .f(s5), .a(s0), .b(s1), .e(s4), .d(s3), .c(s2), .dp(1'b1));
endmodule

module Seg7_Decoder (
  input  i_m3,
  input  i_m2,
  input  i_m1,
  input  i_m0,
  output [7:0] o_seg
);

  wire and_1_out, and_2_out, and_3_out, and_4_out, and_5_out, and_6_out, and_7_out, and_8_out, and_10_out,
       and_11_out, and_12_out, and_13_out, not_1_out, not_2_out, not_3_out, not_4_out;

  not not_1 (not_1_out, i_m3);
  not not_2 (not_2_out, i_m2);
  not not_3 (not_3_out, i_m1);
  not not_4 (not_4_out, i_m0);
  and and_1 (and_1_out, not_1_out, not_2_out, not_3_out);
  and and_2 (and_2_out, i_m2, i_m1, i_m0);
  and and_3 (and_3_out, not_1_out, not_2_out, i_m0);
  and and_4 (and_4_out, not_2_out, i_m1);
  and and_5 (and_5_out, i_m2, not_3_out);
  and and_6 (and_6_out, not_1_out, not_2_out, not_3_out, i_m0);
  and and_7 (and_7_out, i_m2, not_3_out, not_4_out);
  and and_8 (and_8_out, i_m2, i_m1, i_m0);
  and and_9 (o_seg[2], not_2_out, i_m1, not_4_out);
  and and_10 (and_10_out, i_m2, not_3_out, i_m0);
  and and_11 (and_11_out, i_m2, i_m1, not_4_out);
  and and_12 (and_12_out, not_1_out, not_2_out, not_3_out, i_m0);
  and and_13 (and_13_out, i_m2, not_3_out, not_4_out);
  or or_1 (o_seg[6], and_1_out, and_2_out);
  or or_2 (o_seg[5], and_3_out, and_4_out);
  or or_3 (o_seg[4], i_m0, and_5_out);
  or or_4 (o_seg[3], and_6_out, and_7_out, and_8_out);
  or or_5 (o_seg[1], and_10_out, and_11_out);
  or or_6 (o_seg[0], and_12_out, and_13_out);

  assign o_seg[7] = 1'b1;
endmodule

module CircuitA (
  input  i2,
  input  i1,
  input  i0,
  output o2,
  output o1,
  output o0
);

  not not_1 (o1, i1);
  and and_1 (o2, i2, i1);

  assign o0 = i0;
endmodule

module myComparator (
  input  v3,
  input  v2,
  input  v1,
  input  v0,
  output z
);

  wire and_1_out, and_2_out;

  and and_1 (and_1_out, v3, v1);
  and and_2 (and_2_out, v3, v2);
  or or_1 (z, and_1_out, and_2_out);
endmodule

module CircuitB (
  input  z,
  output s6,
  output s5,
  output s4,
  output s3,
  output s2,
  output s1,
  output s0
);


  assign s0 = z;
  assign s1 = 1'b0;
  assign s2 = 1'b0;
  assign s3 = z;
  assign s4 = z;
  assign s5 = z;
  assign s6 = 1'b1;
endmodule

module bit4_adder (
  input  c1,
  input  b0,
  input  a0,
  input  b1,
  input  a1,
  input  b2,
  input  a2,
  input  b3,
  input  a3,
  output s0,
  output s1,
  output s2,
  output s3
);

  wire c1_t, c2, c3, c4;

  full_adder full_adder_1 (.c1(c1), .b(b0), .a(a0), .c0(c1_t), .s(s0));
  full_adder full_adder_2 (.c1(c1_t), .b(b1), .a(a1), .c0(c2), .s(s1));
  full_adder full_adder_3 (.c1(c2), .b(b2), .a(a2), .c0(c3), .s(s2));
  full_adder full_adder_4 (.c1(c3), .b(b3), .a(a3), .c0(c4), .s(s3));
endmodule

module full_adder (
  input  c1,
  input  b,
  input  a,
  output c0,
  output s
);

  wire xor_1_out;

  Multiplexer multiplexer_1 (.in0(c1), .in1(b), .out(c0), .sel(xor_1_out));
  xor xor_1 (xor_1_out, b, a);
  xor xor_2 (s, c1, xor_1_out);
endmodule

module bit4_adder_part5 (
  input  in_1,
  input  [3:0] in_2,
  input  [3:0] in_3
);

  wire bit4_adder_1_s0, bit4_adder_1_s1, bit4_adder_1_s2, bit4_adder_1_s3, circuita_1_o0, circuita_1_o1,
       circuita_1_o2, d0, d1, d2, d3, d4, d5, d6, multiplexer_1_out, multiplexer_2_out, multiplexer_3_out,
       multiplexer_4_out, s0, s1, s2, s3, s4, s5, s6, z;
  wire [7:7] Seg7_Decoder_1_o_seg;

  bit4_adder bit4_adder_1 (
    .c1(in_1), .b0(in_2[0]), .a0(in_3[0]), .b1(in_2[1]), .a1(in_3[1]), .b2(in_2[2]), .a2(in_3[2]),
    .b3(in_2[3]), .a3(in_3[3]), .s0(bit4_adder_1_s0), .s1(bit4_adder_1_s1), .s2(bit4_adder_1_s2),
    .s3(bit4_adder_1_s3));
  CircuitA circuita_1 (
    .i2(bit4_adder_1_s2), .i1(bit4_adder_1_s1), .i0(bit4_adder_1_s0), .o2(circuita_1_o2), .o1(circuita_1_o1),
    .o0(circuita_1_o0));
  Multiplexer multiplexer_1 (.in0(bit4_adder_1_s0), .in1(circuita_1_o0), .out(multiplexer_1_out), .sel(z));
  Multiplexer multiplexer_2 (.in0(bit4_adder_1_s1), .in1(circuita_1_o1), .out(multiplexer_2_out), .sel(z));
  Multiplexer multiplexer_3 (.in0(bit4_adder_1_s2), .in1(circuita_1_o2), .out(multiplexer_3_out), .sel(z));
  Multiplexer multiplexer_4 (.in0(bit4_adder_1_s3), .out(multiplexer_4_out), .sel(z));  // open: in1
  myComparator mycomparator_1 (
    .v3(bit4_adder_1_s3), .v2(bit4_adder_1_s2), .v1(bit4_adder_1_s2), .v0(bit4_adder_1_s0), .z(z));
  Seg7_Decoder Seg7_Decoder_1 (
    .i_m3(multiplexer_4_out), .i_m2(multiplexer_3_out), .i_m1(multiplexer_2_out), .i_m0(multiplexer_1_out),
    .o_seg({Seg7_Decoder_1_o_seg[7], s6, s5, s4, s3, s2, s1, s0}));
  CircuitB CircuitB_1 (.z(z), .s6(d6), .s5(d5), .s4(d4), .s3(d3), .s2(d2), .s1(d1), .s0(d0));
  _7_Segment_Display #(.active("false")) L_7_Segment_Display_1 (
    .g(d6), .f(d5), .a(d0), .b(d1), .e(d4), .d(d3), .c(d2), .dp(1'b1));
  _7_Segment_Display #(.active("false")) L_7_Segment_Display_2 (
    .g(s6), .f(s5), .a(s0), .b(s1), .e(s4), .d(s3), .c(s2), .dp(1'b1));
endmodule
