// Logisim project 8_Bit_Accumulator_Circuit.circ as structural Verilog: 1 circuit, main circuit main
module main (
  input  [7:0] in_1
);

  wire adder_1_cout, CLK, d_ff_1_q, R;
  wire [7:0] A_Register_q, adder_1_out, S_Register_q;

  Button Reset (.out(R));
  Clock clock_1 (.out(CLK));
  Register A_Register (.D(in_1), .en(1'b1), .clk(CLK), .Q(A_Register_q), .clr(R));
  Register S_Register (.D(adder_1_out), .en(1'b1), .clk(CLK), .Q(S_Register_q), .clr(R));
  Adder adder_1 (.a(A_Register_q), .b(S_Register_q), .out(adder_1_out), .cin(1'b0), .cout(adder_1_cout));
  D_Flip_Flop d_ff_1 (.D(adder_1_cout), .clk(CLK), .Q(d_ff_1_q));  // open: Qn, preset, reset
  LED led_1 (.in(d_ff_1_q));
  // Probe on S_Register_q
endmodule
