// Logisim project 8_Bit_Accumulator_Subtractor_Circuit.circ as structural Verilog: 1 circuit, main circuit main
module main (
  input  Add_Sum,
  input  [7:0] in_2
);

  wire adder_1_cout, CLK, d_ff_1_q, R;
  wire [7:0] A_Register_q, adder_1_out, S_Register_q, xor_5_out;

  Button Reset (.out(R));
  Clock clock_1 (.out(CLK));
  Register A_Register (.D(in_2), .en(1'b1), .clk(CLK), .Q(A_Register_q), .clr(R));
  Register S_Register (.D(adder_1_out), .en(1'b1), .clk(CLK), .Q(S_Register_q), .clr(R));
  xor xor_1 (xor_5_out[1], Add_Sum, A_Register_q[1]);
  xor xor_2 (xor_5_out[3], Add_Sum, A_Register_q[3]);
  xor xor_3 (xor_5_out[5], Add_Sum, A_Register_q[5]);
  xor xor_4 (xor_5_out[7], Add_Sum, A_Register_q[7]);
  xor xor_5 (xor_5_out[0], Add_Sum, A_Register_q[0]);
  xor xor_6 (xor_5_out[2], Add_Sum, A_Register_q[2]);
  xor xor_7 (xor_5_out[4], Add_Sum, A_Register_q[4]);
  xor xor_8 (xor_5_out[6], Add_Sum, A_Register_q[6]);
  Adder adder_1 (.a(xor_5_out), .b(S_Register_q), .out(adder_1_out), .cin(Add_Sum), .cout(adder_1_cout));
  D_Flip_Flop d_ff_1 (.D(adder_1_cout), .clk(CLK), .Q(d_ff_1_q), .reset(R));  // open: Qn, preset
  LED led_1 (.in(d_ff_1_q));
  // Probe on S_Register_q

  // Other names for the same wires on the sheet: X = Add_Sum
endmodule
