// Logisim project Multiplier_Circuit.circ as structural Verilog: 2 circuits, main circuit main
module main (
  input  [3:0] A,
  input  [3:0] B,
  output [7:0] P
);

  wire A1, A2, A3, A5, A6, A7, A8, A9, A10, A11, A12, B1, B2, B3, B4, FA1_cout, FA2_cout, FA2S, FA3_cout,
       FA3S, FA4C, FA4S, FA5_cout, FA6_cout, FA6S, FA7_cout, FA7S, FA8C, FA8S, FA9_cout, FA10_cout, FA11_cout;

  and and_1 (A3, A[3], B[0]);
  and and_2 (B4, A[3], B[1]);
  and and_3 (A8, A[3], B[2]);
  and and_4 (A12, A[3], B[3]);
  FullAdder FA1 (.A(A1), .B(B1), .Cin(1'b0), .Sum(P[1]), .Cout(FA1_cout));
  FullAdder FA5 (.A(A5), .B(FA2S), .Cin(1'b0), .Sum(P[2]), .Cout(FA5_cout));
  FullAdder FA9 (.A(A9), .B(FA6S), .Cin(1'b0), .Sum(P[3]), .Cout(FA9_cout));
  and and_5 (A2, A[2], B[0]);
  and and_6 (B3, A[2], B[1]);
  and and_7 (A7, A[2], B[2]);
  and and_8 (A11, A[2], B[3]);
  and and_9 (A1, A[1], B[0]);
  and and_10 (B2, A[1], B[1]);
  and and_11 (A6, A[1], B[2]);
  and and_12 (A10, A[1], B[3]);
  and and_13 (P[0], A[0], B[0]);
  and and_14 (B1, A[0], B[1]);
  and and_15 (A5, A[0], B[2]);
  and and_16 (A9, A[0], B[3]);
  FullAdder FA2 (.A(A2), .B(B2), .Cin(FA1_cout), .Sum(FA2S), .Cout(FA2_cout));
  FullAdder FA6 (.A(A6), .B(FA3S), .Cin(FA5_cout), .Sum(FA6S), .Cout(FA6_cout));
  FullAdder FA10 (.A(A10), .B(FA7S), .Cin(FA9_cout), .Sum(P[4]), .Cout(FA10_cout));
  FullAdder FA3 (.A(A3), .B(B3), .Cin(FA2_cout), .Sum(FA3S), .Cout(FA3_cout));
  FullAdder FA7 (.A(A7), .B(FA4S), .Cin(FA6_cout), .Sum(FA7S), .Cout(FA7_cout));
  FullAdder FA11 (.A(A11), .B(FA8S), .Cin(FA10_cout), .Sum(P[5]), .Cout(FA11_cout));
  FullAdder FA4 (.A(1'b0), .B(B4), .Cin(FA3_cout), .Sum(FA4S), .Cout(FA4C));
  FullAdder FA8 (.A(A8), .B(FA4C), .Cin(FA7_cout), .Sum(FA8S), .Cout(FA8C));
  FullAdder FA12 (.A(A12), .B(FA8C), .Cin(FA11_cout), .Sum(P[6]), .Cout(P[7]));
endmodule

module FullAdder (
  input  A,
  input  B,
  input  Cin,
  output Sum,
  output Cout
);

  wire and_1_out, and_2_out, xor_1_out;

  xor xor_1 (xor_1_out, A, B);
  and and_1 (and_1_out, A, B);
  and and_2 (and_2_out, xor_1_out, Cin);
  xor xor_2 (Sum, xor_1_out, Cin);
  or or_1 (Cout, and_1_out, and_2_out);
endmodule
